# Fritzing sketch ArduinoPins (saved by Fritzing 0.8.7b)
breadboards: 1

parts:
  Part1 = Arduino Uno (Rev3)
  C1 = Ceramic Capacitor [capacitance=1µF package="100 mil [THT, multilayer]"]
  C2 = Ceramic Capacitor [capacitance=1µF package="100 mil [THT, multilayer]"]
  R1 = Resistor [tolerance=±5% resistance=22k package=THT]
  R2 = Resistor [tolerance=±5% resistance=22k package=THT]

nets:
  N1: Part1.A1, C1.1, R1.Pin_1
  N2: Part1.A2, C2.1, R2.Pin_1
  N3: Part1.D9_PWM, R1.Pin_0
  N4: Part1.D10_PWM/SS, R2.Pin_0
  N5: Part1.GND, C1.0, C2.0
